# Fritzing sketch CQ_PSoC5LP_PMB_I2C_LCD_AQM1602 (saved by Fritzing 0.9.2b)
breadboards: 1
perfboards: 1

parts:
  U1 = mystery part, 4 pins [chip_label=AQM1602]
  J1 = female pin header, 20 pins [form="♀ (female)"]
  J2 = female pin header, 20 pins [form="♀ (female)"]  # not connected
  J3 = female pin header, 20 pins [form="♀ (female)"]  # not connected
  J4 = female pin header, 20 pins [form="♀ (female)"]

nets:
  N1: U1.pin1, J1.pin19
  N2: U1.pin2, J4.pin1
  N3: U1.pin3, J1.pin1
  N4: U1.pin4, J4.pin19

notes:
  CQ PSoC 5LP PMB
  AQM1602
  1 V+
  2 SCL
  3 SDA
  4 GND
