# Fritzing sketch PSoC5LP_Prototyping_Kit_I2C_LCD_AQM1602 (saved by Fritzing 0.9.2b)
breadboards: 2

parts:
  U1 = mystery part, 4 pins [chip_label=AQM1602]
  U2 = mystery part, 52 pins [chip_label="PSoC 5LP Prototyping Kit"]

nets:
  N1: U1.pin1, U2.pin25
  N2: U1.pin2, U2.pin2
  N3: U1.pin3, U1.pin4, U2.pin26

notes:
  AQM1602
  1 V+
  2 SCL
  3 SDA
  4 GND
